# Fritzing sketch s_03_traffic_pedestrian_signal_schematic (saved by Fritzing 0.8.3b)
breadboards: 1

parts:
  Componente1 = Arduino Uno (Rev3)
  LED1 = LED - 5mm [color="Green (555nm)" package="5 mm [THT]"]
  R1 = Resistor [tolerance=±5% resistance=330 package=THT]
  LED2 = LED - 5mm [color="Yellow (585nm)" package="5 mm [THT]"]
  LED3 = LED - 5mm [color="Red (633nm)" package="5 mm [THT]"]
  R2 = Resistor [tolerance=±5% resistance=330 package=THT]
  R3 = Resistor [tolerance=±5% resistance=330 package=THT]
  LED4 = LED - 5mm [color="Red (633nm)" package="5 mm [THT]"]
  LED5 = LED - 5mm [color="Green (555nm)" package="5 mm [THT]"]
  R4 = Resistor [tolerance=±5% resistance=330 package=THT]
  R5 = Resistor [tolerance=±5% resistance=330 package=THT]
  S1 = Pushbutton [package="[THT]"]
  R6 = Resistor [tolerance=±5% resistance=1k package=THT]

nets:
  N1: Componente1.ICSP_MISO, Componente1.D12/MISO, LED1.anode
  N2: Componente1.GND, R1.Pin_0, R2.Pin_0, R3.Pin_0, R4.Pin_0, R5.Pin_0, R6.Pin_1
  N3: Componente1.D8, LED2.anode
  N4: Componente1.D9_PWM, S1.Pin_3, S1.Pin_4
  N5: Componente1.D2, LED4.anode
  N6: Componente1.D4, LED5.anode
  N7: Componente1.D7, LED3.anode
  N8: LED1.cathode, R3.Pin_1
  N9: R1.Pin_1, LED3.cathode
  N10: LED2.cathode, R2.Pin_1
  N11: LED4.cathode, R5.Pin_1
  N12: LED5.cathode, R4.Pin_1
  N13: S1.Pin_1, S1.Pin_2, R6.Pin_0
