# Fritzing sketch s_04_binary_clock_schematic (saved by Fritzing 0.8.3b)
breadboards: 1

parts:
  Componente1 = Arduino Uno (Rev3)
  LED1 = LED - 5mm [color="Red (633nm)" package="5 mm [THT]"]
  LED2 = LED - 5mm [color="Red (633nm)" package="5 mm [THT]"]
  LED3 = LED - 5mm [color="Red (633nm)" package="5 mm [THT]"]
  LED4 = LED - 5mm [color="Red (633nm)" package="5 mm [THT]"]
  LED5 = LED - 5mm [color="Red (633nm)" package="5 mm [THT]"]
  LED6 = LED - 5mm [color="Red (633nm)" package="5 mm [THT]"]
  LED7 = LED - 5mm [color="Red (633nm)" package="5 mm [THT]"]
  R1 = Resistor [tolerance=±5% resistance=330 package=THT]
  R8 = Resistor [tolerance=±5% resistance=330 package=THT]
  R9 = Resistor [tolerance=±5% resistance=330 package=THT]
  R10 = Resistor [tolerance=±5% resistance=330 package=THT]
  R11 = Resistor [tolerance=±5% resistance=330 package=THT]
  R12 = Resistor [tolerance=±5% resistance=330 package=THT]
  R13 = Resistor [tolerance=±5% resistance=330 package=THT]
  LED8 = LED - 5mm [color="Green (565nm)" package="5 mm [THT]"]
  LED9 = LED - 5mm [color="Green (565nm)" package="5 mm [THT]"]
  LED10 = LED - 5mm [color="Green (565nm)" package="5 mm [THT]"]
  LED11 = LED - 5mm [color="Green (565nm)" package="5 mm [THT]"]
  LED12 = LED - 5mm [color="Green (565nm)" package="5 mm [THT]"]
  LED13 = LED - 5mm [color="Green (565nm)" package="5 mm [THT]"]
  LED14 = LED - 5mm [color="Green (565nm)" package="5 mm [THT]"]
  R14 = Resistor [tolerance=±5% resistance=360 package=THT]
  R15 = Resistor [tolerance=±5% resistance=360 package=THT]
  R16 = Resistor [tolerance=±5% resistance=360 package=THT]
  R17 = Resistor [tolerance=±5% resistance=360 package=THT]
  R18 = Resistor [tolerance=±5% resistance=360 package=THT]
  R19 = Resistor [tolerance=±5% resistance=360 package=THT]
  R20 = Resistor [tolerance=±5% resistance=360 package=THT]
  LED15 = LED - 5mm [color="Yellow (585nm)" package="5 mm [THT]"]
  LED16 = LED - 5mm [color="Yellow (585nm)" package="5 mm [THT]"]
  LED17 = LED - 5mm [color="Yellow (585nm)" package="5 mm [THT]"]
  LED18 = LED - 5mm [color="Yellow (585nm)" package="5 mm [THT]"]
  LED19 = LED - 5mm [color="Yellow (585nm)" package="5 mm [THT]"]
  LED20 = LED - 5mm [color="Yellow (585nm)" package="5 mm [THT]"]
  R21 = Resistor [tolerance=±5% resistance=360 package=THT]
  R22 = Resistor [tolerance=±5% resistance=360 package=THT]
  R23 = Resistor [tolerance=±5% resistance=360 package=THT]
  R24 = Resistor [tolerance=±5% resistance=360 package=THT]
  R25 = Resistor [tolerance=±5% resistance=360 package=THT]
  R26 = Resistor [tolerance=±5% resistance=360 package=THT]

nets:
  N1: Componente1.A0, R26.Pin_1
  N2: Componente1.A1, R25.Pin_1
  N3: Componente1.A2, R24.Pin_1
  N4: Componente1.A3, R23.Pin_1
  N5: Componente1.A4/SDA, R22.Pin_1
  N6: Componente1.A5/SCL, R21.Pin_1
  N7: Componente1.GND, LED1.cathode, LED2.cathode, LED3.cathode, LED4.cathode, LED5.cathode, LED6.cathode, LED7.cathode, LED8.cathode, LED9.cathode, LED10.cathode, LED11.cathode, LED12.cathode, LED13.cathode, LED14.cathode, LED15.cathode, LED16.cathode, LED17.cathode, LED18.cathode, LED19.cathode, LED20.cathode
  N8: Componente1.D8, R18.Pin_1
  N9: Componente1.D9_PWM, R17.Pin_1
  N10: Componente1.D10_PWM/SS, R16.Pin_1
  N11: Componente1.D11_PWM/MOSI, R15.Pin_1
  N12: Componente1.D12/MISO, R20.Pin_1
  N13: Componente1.D13/SCK, R19.Pin_1
  N14: Componente1.D0/RX, R1.Pin_1
  N15: Componente1.D1/TX, R10.Pin_1
  N16: Componente1.D2, R9.Pin_1
  N17: Componente1.D3_PWM, R12.Pin_1
  N18: Componente1.D4, R13.Pin_1
  N19: Componente1.D5_PWM, R8.Pin_1
  N20: Componente1.D6_PWM, R11.Pin_1
  N21: Componente1.D7, R14.Pin_1
  N22: LED1.anode, R1.Pin_0
  N23: LED2.anode, R11.Pin_0
  N24: LED3.anode, R8.Pin_0
  N25: LED4.anode, R13.Pin_0
  N26: LED5.anode, R9.Pin_0
  N27: LED6.anode, R10.Pin_0
  N28: LED7.anode, R12.Pin_0
  N29: LED8.anode, R14.Pin_0
  N30: LED9.anode, R19.Pin_0
  N31: LED10.anode, R20.Pin_0
  N32: LED11.anode, R15.Pin_0
  N33: LED12.anode, R16.Pin_0
  N34: LED13.anode, R17.Pin_0
  N35: LED14.anode, R18.Pin_0
  N36: LED15.anode, R26.Pin_0
  N37: LED16.anode, R21.Pin_0
  N38: LED17.anode, R22.Pin_0
  N39: LED18.anode, R23.Pin_0
  N40: LED19.anode, R24.Pin_0
  N41: LED20.anode, R25.Pin_0

notes:
  Hours
  Minutes
  Seconds
